# Fritzing sketch HC_SR04 Ultrasonic Distance Sensor (saved by Fritzing 0.9.3b)
breadboards: 1

parts:
  hc-sr1 = hc-sr04
  Raspberry_Pi1 = Raspberry Pi 2
  R1 = Resistor [tolerance=±5% resistance=2.2k package="1206 [SMD]"]
  R5 = Resistor [tolerance=±5% resistance=1k package="1206 [SMD]"]

nets:
  VCC: hc-sr1.VCC, Raspberry_Pi1.5V
  N1: hc-sr1.Trig, Raspberry_Pi1.GPIO12
  N2: hc-sr1.Echo, R1.Pin_0, R5.Pin_0
  GND: hc-sr1.GND, Raspberry_Pi1.GND, R1.Pin_1
  N3: Raspberry_Pi1.GPIO16, R5.Pin_1

notes:
  NOTE the HC-SR04 requires 5 volts and the echo pin outputs 5 volts so you need a voltage divider to drop the voltage to 3.3 volts for the Raspberry Pi
