# Fritzing sketch ML8511Demo (saved by Fritzing 0.9.3b)
breadboards: 1

parts:
  IC1 = MCP3008 8-channel 10-bit ADC [part_number=MCP3008]
  Raspberry_Pi1 = Raspberry Pi 2
  Part1 = ML8511 Breakout Board
  Part2 = ML8511 Breakout Board

nets:
  N1: IC1.no_name_yet#1, Part2.OUT
  N2: IC1.no_name_yet#2, Part1.OUT
  GND: IC1.no_name_yet#9, IC1.no_name_yet#14, Raspberry_Pi1.GND, Part1.GND, Part2.GND
  N3: IC1.no_name_yet#10, Raspberry_Pi1.GPIO8
  N4: IC1.no_name_yet#11, Raspberry_Pi1.GPIO10
  N5: IC1.no_name_yet#12, Raspberry_Pi1.GPIO9
  N6: IC1.no_name_yet#13, Raspberry_Pi1.GPIO11
  3V3: IC1.no_name_yet#15, IC1.no_name_yet#16, Raspberry_Pi1.3v3, Raspberry_Pi1.3V3, Part1.VIN, Part2.VIN
  N7: Part2.3V3, Part2.EN

custom parts:
  ML8511 Breakout Board: This breakout board uses the ML8511 UV (ultraviolet) light sensor. The ML8511 works best with light in the 280-390nm wavelengths. The board operates at 2.7 to 3.6V.
